// Logisim project clock_sim.circ as structural Verilog: 1 circuit, main circuit main
module main (
);

  wire and_1_out, and_2_out, and_3_out, and_4_out, clock_1_out, counter_1_carry, counter_3_carry,
       counter_5_carry, d_ff_1_q, d_ff_2_q, d_ff_3_q;
  wire [3:0] counter_1_q, counter_2_q, counter_4_q, counter_6_q;

  Clock clock_1 (.out(clock_1_out));
  Hex_Digit_Display hex_digit_display_1 (.value(counter_2_q));  // open: dp
  Counter #(.max('hf), .width(4)) counter_1 (
    .clr(and_1_out), .clk(clock_1_out), .carry(counter_1_carry), .Q(counter_1_q));  // open: load, up, count, D
  Hex_Digit_Display hex_digit_display_2 (.value(counter_1_q));  // open: dp
  D_Flip_Flop d_ff_1 (.D(counter_1_carry), .clk(clock_1_out), .Q(d_ff_1_q));  // open: Qn, preset, reset
  Counter #(.max('hf), .width(4)) counter_2 (
    .clr(and_1_out), .clk(d_ff_1_q), .Q(counter_2_q));  // open: load, up, count, D, carry
  and and_1 (and_1_out, counter_2_q[1], counter_2_q[0], counter_1_q[1]);
  and and_2 (and_2_out, counter_2_q[1], counter_2_q[0], counter_1_q[0]);
  // Probe on and_2_out
  Counter #(.max('h9), .width(4)) counter_3 (
    .clk(and_2_out), .carry(counter_3_carry));  // open: clr, load, up, count, D, Q
  D_Flip_Flop d_ff_2 (.D(counter_3_carry), .clk(and_2_out), .Q(d_ff_2_q));  // open: Qn, preset, reset
  Counter #(.max('h9), .width(4)) counter_4 (
    .clr(and_3_out), .clk(d_ff_2_q), .Q(counter_4_q));  // open: load, up, count, D, carry
  Counter #(.max('h9), .width(4)) counter_5 (
    .clk(and_3_out), .carry(counter_5_carry));  // open: clr, load, up, count, D, Q
  D_Flip_Flop d_ff_3 (.D(counter_5_carry), .clk(and_3_out), .Q(d_ff_3_q));  // open: Qn, preset, reset
  and and_3 (and_3_out, counter_4_q[1], counter_4_q[2]);
  Counter #(.max('h9), .width(4)) counter_6 (
    .clr(and_4_out), .clk(d_ff_3_q), .Q(counter_6_q));  // open: load, up, count, D, carry
  and and_4 (and_4_out, counter_6_q[1], counter_6_q[2]);
endmodule
